# Fritzing sketch kevFitz (saved by Fritzing 0.9.3b)
breadboards: 1

parts:
  Part1 = RFID-RC522-v2
  Part2 = Arduino Uno (Rev3)
  LED1 = LED - 5mm [color="Red (633nm)" package="5 mm [THT]"]
  R1 = Resistor [tolerance=±5% resistance=220 package=THT]
  R2 = Resistor [tolerance=±5% resistance=220 package=THT]
  LED2 = smd LED [color="Green (565nm)" package="0603 [SMD]"]

nets:
  GND: Part1.GND, Part2.GND, LED1.cathode, LED2.cathode
  N1: Part1.RST, Part2.D9_PWM
  3.3V: Part1.3.3V, Part2.3V3
  N2: Part2.D5_PWM, R2.Pin_0
  N3: Part2.D6_PWM, R1.Pin_1
  N4: LED1.anode, R1.Pin_0
  N5: R2.Pin_1, LED2.anode

custom parts:
  RFID-RC522-v2: A simple China made RFID-RC522 Reader; do check the pin labels, as this is a MFRC522 based clone.

// code stored in the sketch: nfc.ino
//Viral Science
//RFID
#include <SPI.h>
#include <MFRC522.h>

 
#define SS_PIN 10
#define RST_PIN 9

MFRC522 mfrc522(SS_PIN, RST_PIN);   // Create MFRC522 instance.
char myStrings[]={"chocolate,1.00,2,tesco"};

 
void setup() 
{
  Serial.begin(9600);   // Initiate a serial communication
  SPI.begin();      // Initiate  SPI bus
  mfrc522.PCD_Init();
  pinMode(6, OUTPUT);// Initiate MFRC522
  //Serial.println("Put your card to the reader...");
 // Serial.println();
  

}
void loop() 
{ 

   while(Serial.available()> 0){
    int sdata = Serial.read();
    Serial.println("here is the data " +sdata );
    
    if(sdata == 0x01){
      digitalWrite(6, HIGH);
     delay(1000);
     digitalWrite(6,LOW);
      }
  }
  // Look for new cards
  if ( ! mfrc522.PICC_IsNewCardPresent()) 
  {
    return;
  }
  // Select one of the cards
  if ( ! mfrc522.PICC_ReadCardSerial()) 
  {
    return;
  }

  String content= "";
  byte letter;
  for (byte i = 0; i < mfrc522.uid.size; i++) 
  {
   
     content.concat(String(mfrc522.uid.uidByte[i] < 0x10 ? " 0" : " "));
     content.concat(String(mfrc522.uid.uidByte[i], HEX));
  }
  content.toUpperCase();

      
  
  if (content.substring(1) == "E7 51 55 C5") //change here the UID of the card/cards that you want to give access
  {
   
  
     Serial.println(myStrings);
   //delay(500);
  // }
    delay(500);
  }

   else   {
    Serial.println(" Access denied");
    delay(1000);

  }
  
   
 

}
